# Fritzing sketch Schema tapis (saved by Fritzing 0.9.3b)
breadboards: 1

parts:
  Composant1 = Arduino BT
  R1 = Resistor [tolerance=±5% resistance=220 package=THT]
  R2 = Resistor [tolerance=±5% resistance=220 package=THT]
  LED1 = LED - 5mm [color="Red (633nm)" package="5 mm [THT]"]
  LED2 = LED - 5mm [color="Red (633nm)" package="5 mm [THT]"]
  R3 = Resistor [tolerance=±5% resistance=1M package="2512 [SMD]"]
  R4 = Resistor [tolerance=±5% resistance=1M package="2512 [SMD]"]  # not connected
  S1 = Textile Pushbutton [part_number="TACRACPS1X0404GY "]
  S2 = Textile Pushbutton [part_number="TACRACPS1X0404GY "]

nets:
  N1: Composant1.D8, S2.leg0
  N2: Composant1.MISO/D12, LED2.cathode
  N3: Composant1.GND, R1.Pin_1, R2.Pin_0
  N4: Composant1.D2, R3.Pin_1, S1.leg0
  N5: Composant1.D4, R3.Pin_0
  N6: Composant1.PWM_D5, LED1.anode
  N7: R1.Pin_0, LED1.cathode
  N8: R2.Pin_1, LED2.anode
